# Fritzing sketch interrupt fritzing (saved by Fritzing 0.9.3b)
breadboards: 2

parts:
  U1 = PIC16F874A
  XTAL1 = Crystal [frequency="16 Mhz" package=THT]
  U2 = LCD-16X2 [package=lcd-16x2]
  U3 = POT [package=pot_mammoth]
  RY1 = srd-05vdc-sl-c_1
  VCC1 = Battery block 9V  # not connected
  Q1 = NPN-Transistor [package="TO92 [THT]"]
  signal = Resistor [tolerance=±5% resistance=1k package=THT]
  kEYPAD_MATRICIAL_2 = KEYPAD_4x3

nets:
  N1: U1.connector10, U1.connector31, U2.VDD, U2.A, U3.S, RY1.connector4
  N2: U1.connector11, U1.connector12, U1.connector30, XTAL1.pin_1, U2.VSS, U2.R_W, U2.K, U3.E
  N3: U1.connector13, XTAL1.pin_0
  N4: U1.connector14, U2.DB4
  N5: U1.connector15, U2.DB5
  N6: U1.connector16, U2.DB6
  N7: U1.connector17, U2.DB7
  N8: U1.connector18, kEYPAD_MATRICIAL_2.connector27
  N9: U1.connector19, kEYPAD_MATRICIAL_2.connector25
  N10: U1.connector20, kEYPAD_MATRICIAL_2.connector29
  N11: U1.connector23, U2.E
  N12: U1.connector26, kEYPAD_MATRICIAL_2.connector26
  N13: U1.connector27, kEYPAD_MATRICIAL_2.connector31
  N14: U1.connector28, kEYPAD_MATRICIAL_2.connector30
  N15: U1.connector29, kEYPAD_MATRICIAL_2.connector28
  N16: U2.VO, U3.A
  N17: Q1.C, signal.Pin_1
